# Fritzing sketch circuito tinaco (saved by Fritzing 0.9.3b)
circuit board: 6.04073cm x 8.13515cm
breadboards: 1

parts:
  R2 = Resistor [tolerance=±5% resistance=220k package=THT]
  R3 = Resistor [tolerance=±5% resistance=220k package=THT]
  R4 = Resistor [tolerance=±5% resistance=220k package=THT]
  R5 = Resistor [tolerance=±5% resistance=220k package=THT]
  R6 = Resistor [tolerance=±5% resistance=220k package=THT]
  U2 = RJ45 Jack [package=rj45-8]
  R1 = Resistor [tolerance=±10% resistance=220k package=THT]
  J1 = female pin header, 2 pins [form="♀ (female)"]
  Q1 = PNP-Transistor [package="TO92 [THT]"]
  J2 = Screw terminal - 2 pins [package=THT]
  XTAL1 = Crystal [frequency="16 Mhz" package=THT]
  C1 = Ceramic Capacitor [capacitance=100nF package="100 mil [THT, multilayer]"]
  C2 = Ceramic Capacitor [capacitance=100nF package="100 mil [THT, multilayer]"]
  C3 = Electrolytic Capacitor [capacitance=1µF package="100 mil [THT, electrolytic]"]
  LED1 = LED - 5mm [color="Red (633nm)" package="5 mm [THT]"]
  R7 = Resistor [tolerance=±5% resistance=220 package=THT]
  R8 = Resistor [tolerance=±5% resistance=10k package=THT]
  R9 = Resistor [tolerance=±5% resistance=10k package=THT]
  K1 = OMRON PCB Power Relay – G5LE [part_number="G5LE-1\n" package=THT]
  T1_-_~G_-_T2 = screw terminal, 3 pins
  J3 = female pin header, 6 pins [form="♀ (female)"]
  LED2 = LED - 5mm [color="Red (633nm)" package="5 mm [THT]"]
  R10 = Resistor [tolerance=±5% resistance=220 package=THT]
  U3 = atmega328 [package=dip]
  J4 = female pin header, 2 pins [form="♀ (female)"]
  R11 = Resistor [tolerance=±5% resistance=10k package=THT]
  J5 = female pin header, 2 pins [form="♀ (female)"]
  R12 = Resistor [tolerance=±5% resistance=10k package=THT]
  J6 = female pin header, 2 pins [form="♀ (female)"]
  J7 = female pin header, 2 pins [form="♀ (female)"]
  R13 = Resistor [tolerance=±5% resistance=10k package=THT]
  R14 = Resistor [tolerance=±5% resistance=10k package=THT]

nets:
  N1: R2.Pin_0, U2.3, U3.D0_(RX)
  N2: R2.Pin_1, R3.Pin_1, R4.Pin_1, R5.Pin_1, R6.Pin_1, R1.Pin_1, J2.pin1, C1.0, C2.0, C3.-, LED1.cathode, K1.COIL1, LED2.cathode, U3.VCC, U3.AREF, R11.Pin_1, R12.Pin_1, R13.Pin_0, R14.Pin_0
  N3: R3.Pin_0, U2.4, U3.D1_(TX)
  N4: R4.Pin_0, U2.5, U3.D2
  N5: R5.Pin_0, U2.6, U3.D3_(PWM)
  N6: R6.Pin_0, U2.7, U3.D4
  N7: U2.1, J1.pin1, R9.Pin_0
  N8: R1.Pin_0, J1.pin2, U3.RESET
  N9: Q1.E, J2.pin2, C3.+, U3.XLAT1, U3.GND, J4.pin2, J5.pin1
  N10: Q1.B, R8.Pin_0
  N11: Q1.C, R9.Pin_1
  N12: XTAL1.pin_0, C1.1, U3.AVCC
  N13: XTAL1.pin_1, C2.1, U3.D13
  N14: LED1.anode, R10.Pin_0
  N15: R7.Pin_0, LED2.anode
  N16: R7.Pin_1, U3.D11_(PWM)
  N17: R8.Pin_1, U3.A2
  N18: K1.A, T1_-_~G_-_T2.pin3
  N19: K1.C, T1_-_~G_-_T2.pin2
  N20: K1.COIL2, U3.D12
  N21: K1.B, T1_-_~G_-_T2.pin1
  N22: J3.pin1, U3.D9_(PWM)
  N23: J3.pin2, U3.D8
  N24: J3.pin3, U3.D7
  N25: J3.pin4, U3.D6_(PWM)
  N26: J3.pin5, U3.D5_(PWM)
  N27: J3.pin6, U3.XLAT2
  N28: R10.Pin_1, U3.D10_(PWM)
  N29: U3.A0, J4.pin1, R11.Pin_0
  N30: U3.A1, J5.pin2, R12.Pin_0
  N31: U3.A3, J6.pin2
  N32: U3.A4, J6.pin1
  N33: J7.pin1, R14.Pin_1
  N34: J7.pin2, R13.Pin_1
